# Fritzing sketch carro (saved by Fritzing 0.9.0b)
breadboards: 1

parts:
  Parte1 = Arduino Uno (Rev3)
  IC1 = L293D [package=THT]
  M1 = DC Motor
  M2 = DC Motor
  U3 = generic_sip_4_300mil.fzp [chip_label=IC]
  U4 = generic_sip_4_300mil.fzp [chip_label=IC]

nets:
  N1: Parte1.D8, U3.connector2
  N2: Parte1.D9_PWM, U4.connector1
  N3: Parte1.D10_PWM/SS, U4.connector2
  N4: Parte1.D2, IC1.In_1
  N5: Parte1.D3_PWM, IC1.In_2
  N6: Parte1.D4, IC1.In_4
  N7: Parte1.D5_PWM, IC1.In_3
  N8: Parte1.D7, U3.connector1
  N9: Parte1.5V, IC1.+V, U3.connector0, U4.connector0
  N10: Parte1.GND, IC1.0V, U3.connector3, U4.connector3
  N11: IC1.Out_1_(_Controlled_by_Enable_1_), M2.pin_1
  N12: IC1.Out_2_(_Controlled_by_Enable_1_), M2.pin_2
  N13: IC1.Out_3_(_Controlled_by_Enable_2_), M1.pin_2
  N14: IC1.Out_4_(_Controlled_by_Enable_2_), M1.pin_1
