# Fritzing sketch estacionamiento (saved by Fritzing 0.9.0b)
breadboards: 1

parts:
  Parte1 = Arduino Uno (Rev3)
  S1 = Pushbutton [package="[THT]"]
  S2 = Pushbutton [package="[THT]"]
  R1 = Resistor [tolerance=±5% resistance=220 package=THT]
  R2 = Resistor [tolerance=±5% resistance=220 package=THT]
  J1 = Basic Servo
  U1 = 7-SEGMENT-DISPLAY [package=7-segment-display]

nets:
  N1: Parte1.D8, S2.Pin_1, S2.Pin_2
  N2: Parte1.D9_PWM, S1.Pin_1, S1.Pin_2
  N3: Parte1.D0/RX, U1.E
  N4: Parte1.D1/TX, U1.G
  N5: Parte1.D2, U1.D
  N6: Parte1.D3_PWM, U1.G1
  N7: Parte1.D4, U1.DP
  N8: Parte1.D5_PWM, U1.A
  N9: Parte1.D6_PWM, U1.G2
  5V: Parte1.5V, J1.vcc
  GND: Parte1.GND, S1.Pin_3, S1.Pin_4, S2.Pin_3, S2.Pin_4, R1.Pin_0, R2.Pin_0, J1.gnd
  N10: R1.Pin_1, U1.C
  N11: R2.Pin_1, U1.F
